# Fritzing sketch birdhouse-esp8266 (saved by Fritzing 0.9.9b)
circuit board: 3.96694cm x 5.5265cm
breadboards: 1

parts:
  WeMos_D1_Mini1 = WeMos D1 Mini
  DFRobot_DFPlayer_Mini1 = DFRobot DFPlayer Mini [part_number=DFR0299]
  SPKR1 = Loudspeaker
  PIR_sensor = screw terminal, 3 pins
  R1 = Resistor [tolerance=±5% resistance=1k package=THT]

nets:
  5V: WeMos_D1_Mini1.5V, DFRobot_DFPlayer_Mini1.VCC, PIR_sensor.pin2
  N1: WeMos_D1_Mini1.D5, DFRobot_DFPlayer_Mini1.TX
  N2: WeMos_D1_Mini1.D6, R1.Pin_0
  N3: WeMos_D1_Mini1.D7, PIR_sensor.pin3
  N4: WeMos_D1_Mini1.G, DFRobot_DFPlayer_Mini1.GND-1, DFRobot_DFPlayer_Mini1.GND-2, PIR_sensor.pin1
  N5: DFRobot_DFPlayer_Mini1.RX, R1.Pin_1
  N6: DFRobot_DFPlayer_Mini1.SPK_1, SPKR1.pin2
  N7: DFRobot_DFPlayer_Mini1.SPK_2, SPKR1.pin1

notes:
  PIR
  SPK
  GND
  SIG
  Birdhouse-ESP8266
  2022 v1
  +
  -
  R1
